// Digital circuit 4_bit_adder.dig as structural Verilog
module _4_bit_adder (
  input  carry_in,
  input  [3:0] b,
  input  [3:0] a,
  output out_0,
  output out_1,
  output out_2,
  output out_3,
  output carry_out
);

  wire full_adder_2_carry_out, full_adder_3_carry_out, full_adder_4_carry_out;

  Full_adder full_adder_1 (.carry_in(full_adder_2_carry_out), .b(b[3]), .a(a[3]), .sum(out_3), .carry_out(carry_out));
  Full_adder full_adder_2 (
    .carry_in(full_adder_3_carry_out), .b(b[2]), .a(a[2]), .sum(out_2), .carry_out(full_adder_2_carry_out));
  Full_adder full_adder_3 (
    .carry_in(full_adder_4_carry_out), .b(b[1]), .a(a[1]), .sum(out_1), .carry_out(full_adder_3_carry_out));
  Full_adder full_adder_4 (.carry_in(carry_in), .b(b[0]), .a(a[0]), .sum(out_0), .carry_out(full_adder_4_carry_out));
endmodule
